// Logisim project Demultiplexador.circ as structural Verilog: 1 circuit, main circuit Demultiplexador
module Demultiplexador (
  input  [2:0] SELETOR,
  input  IN,
  output A,
  output B,
  output C,
  output D,
  output E,
  output F,
  output G,
  output H
);

  Demultiplexer #(.select(3)) demultiplexer_1 (
    .out0(A), .out1(B), .out2(C), .out3(D), .out4(E), .out5(F), .out6(G), .out7(H), .in(IN), .sel(SELETOR));  // open: en
endmodule
