// Logisim project FlipFlop D.circ as structural Verilog: 1 circuit, main circuit FF D
module FF_D (
  input  D,
  input  PRESET,
  input  CLEAR,
  output Q
);

  wire clock_1_out;

  Clock clock_1 (.out(clock_1_out));
  D_Flip_Flop d_ff_1 (.clk(clock_1_out), .D(D), .Q(Q), .preset(PRESET), .reset(CLEAR));  // open: Qn, en
endmodule
