// Logisim project Multiplexador.circ as structural Verilog: 1 circuit, main circuit Multiplexador
module Multiplexador (
  input  [2:0] SELETOR,
  input  A,
  input  B,
  input  C,
  input  D,
  input  E,
  input  F,
  input  G,
  input  H,
  output OUT
);

  Multiplexer #(.select(3)) multiplexer_1 (
    .in0(A), .in1(B), .in2(C), .in3(D), .in4(E), .in5(F), .in6(G), .in7(H), .out(OUT), .sel(SELETOR));  // open: en
endmodule
